# Fritzing sketch BikeNav (saved by Fritzing 0.9.2b)
circuit board: 5.2cm x 5.2cm

parts:
  R18 = PHOTOCELL [package=photocell]
  HC-06 = female pin header, 4 pins [form="♀ (female)"]
  J1 = female pin header, 2 pins [form="♀ (female)"]
  R2 = Resistor [tolerance=±5% resistance=220 package="0603 [SMD]"]
  R1 = Resistor [tolerance=±5% resistance=220 package="0603 [SMD]"]
  R3 = Resistor [tolerance=±5% resistance=220 package="0603 [SMD]"]
  R4 = Resistor [tolerance=±5% resistance=220 package="0603 [SMD]"]
  R5 = Resistor [tolerance=±5% resistance=220 package="0603 [SMD]"]
  LED1 = smd LED [color="Blue (505nm)" package="0805 [SMD]"]
  LED2 = smd LED [color="Blue (505nm)" package="0805 [SMD]"]
  LED4 = smd LED [color="Blue (505nm)" package="0805 [SMD]"]
  LED3 = smd LED [color="Blue (505nm)" package="0805 [SMD]"]
  LED7 = smd LED [color="Blue (505nm)" package="0805 [SMD]"]
  U5 = 74HC595 SMD [package="SO16 [SMD]"]
  U4 = 74HC595 SMD [package="SO16 [SMD]"]
  LED6 = smd LED [color="Blue (505nm)" package="0805 [SMD]"]
  R7 = Resistor [tolerance=±5% resistance=220 package="0603 [SMD]"]
  R8 = Resistor [tolerance=±5% resistance=220 package="0603 [SMD]"]
  LED8 = smd LED [color="Blue (505nm)" package="0805 [SMD]"]
  R6 = Resistor [tolerance=±5% resistance=220 package="0603 [SMD]"]
  LED5 = smd LED [color="Blue (505nm)" package="0805 [SMD]"]
  SSD136 = female pin header, 4 pins [form="♀ (female)"]
  R9 = Resistor [tolerance=±5% resistance=220 package="0603 [SMD]"]
  LED14 = smd LED [color="Blue (505nm)" package="0805 [SMD]"]
  LED15 = smd LED [color="Blue (505nm)" package="0805 [SMD]"]
  LED16 = smd LED [color="Blue (505nm)" package="0805 [SMD]"]
  R16 = Resistor [tolerance=±5% resistance=220 package="0603 [SMD]"]
  R15 = Resistor [tolerance=±5% resistance=220 package="0603 [SMD]"]
  R14 = Resistor [tolerance=±5% resistance=220 package="0603 [SMD]"]
  R13 = Resistor [tolerance=±5% resistance=220 package="0603 [SMD]"]
  R12 = Resistor [tolerance=±5% resistance=220 package="0603 [SMD]"]
  R11 = Resistor [tolerance=±5% resistance=220 package="0603 [SMD]"]
  R10 = Resistor [tolerance=±5% resistance=220 package="0603 [SMD]"]
  LED13 = smd LED [color="Blue (505nm)" package="0805 [SMD]"]
  LED12 = smd LED [color="Blue (505nm)" package="0805 [SMD]"]
  LED11 = smd LED [color="Blue (505nm)" package="0805 [SMD]"]
  LED10 = smd LED [color="Blue (505nm)" package="0805 [SMD]"]
  LED9 = smd LED [color="Blue (505nm)" package="0805 [SMD]"]
  C1 = Ceramic Capacitor [capacitance=22pF package="0603 [SMD, multilayer]"]
  C2 = Ceramic Capacitor [capacitance=22pF package="0603 [SMD, multilayer]"]
  U6 = ATmega328 [package=tqfp]
  XTAL1 = Crystal [frequency="16 Mhz" package=SMD]
  R19 = Resistor [tolerance=±5% resistance=1k package="0603 [SMD]"]
  R17 = Resistor [tolerance=±5% resistance=10k package="0603 [SMD]"]
  X1 = USB Connectors [package=usb-minib]
  Pad1 = Pad [width=2 height=5 connect=center]
  Pad2 = Pad [width=2 height=5 connect=center]

nets:
  VCC: R18.P$1, HC-06.pin4, J1.pin1, U5.MR, U5.VCC, U4.MR, U4.VCC, SSD136.pin2, U6.VCC, U6.AVCC, U6.AREF, R17.Pin_0, Pad2.pad
  N1: R18.P$2, U6.PC0(ADC0), R19.Pin_1
  N2: HC-06.pin1, U6.PD1(TXD)
  N3: HC-06.pin2, U6.PD0(RXD)
  GND: HC-06.pin3, J1.pin2, LED1.cathode, LED2.cathode, LED4.cathode, LED3.cathode, LED7.cathode, U5.GND, U5.OE, U4.GND, U4.OE, LED6.cathode, LED8.cathode, LED5.cathode, SSD136.pin1, LED14.cathode, LED15.cathode, LED16.cathode, LED13.cathode, LED12.cathode, LED11.cathode, LED10.cathode, LED9.cathode, C1.0, C2.0, U6.GND, U6.AGND, R19.Pin_0, X1.GND
  N4: R2.Pin_0, U5.Q6
  N5: R2.Pin_1, LED2.anode
  N6: R1.Pin_0, U5.Q7
  N7: R1.Pin_1, LED1.anode
  N8: R3.Pin_0, U5.Q4
  N9: R3.Pin_1, LED4.anode
  N10: R4.Pin_0, U5.Q5
  N11: R4.Pin_1, LED3.anode
  N12: R5.Pin_0, U5.Q3
  N13: R5.Pin_1, LED5.anode
  N14: LED7.anode, R8.Pin_1
  N15: U5.Q1, R8.Pin_0
  N16: U5.Q2, R7.Pin_0
  N17: U5.Q7', U4.DS
  N18: U5.SH_CP, U4.SH_CP, U6.PB5(SCK)
  N19: U5.ST_CP, U4.ST_CP, U6.PB0(ICP)
  N20: U5.DS, U6.PB3(MOSI_OC2)
  N21: U5.Q0, R6.Pin_0
  N22: U4.Q1, R15.Pin_0
  N23: U4.Q2, R14.Pin_0
  N24: U4.Q3, R13.Pin_0
  N25: U4.Q4, R12.Pin_0
  N26: U4.Q5, R11.Pin_0
  N27: U4.Q6, R10.Pin_0
  N28: U4.Q7, R9.Pin_0
  N29: U4.Q0, R16.Pin_0
  N30: LED6.anode, R7.Pin_1
  N31: LED8.anode, R6.Pin_1
  N32: SSD136.pin3, U6.PC5(ADC5_SCL)
  N33: SSD136.pin4, U6.PC4(ADC4_SDA)
  N34: R9.Pin_1, LED9.anode
  N35: LED14.anode, R14.Pin_1
  N36: LED15.anode, R15.Pin_1
  N37: LED16.anode, R16.Pin_1
  N38: R13.Pin_1, LED13.anode
  N39: R12.Pin_1, LED12.anode
  N40: R11.Pin_1, LED11.anode
  N41: R10.Pin_1, LED10.anode
  N42: C1.1, U6.PB6(XTAL1_TOSC1), XTAL1.pin_0
  N43: C2.1, U6.PB7(XTAL2_TOSC2), XTAL1.pin_1
  N44: U6.PC6(_RESET), R17.Pin_1
  N45: X1.VBUS, Pad1.pad

notes:
  BikeNav Ver. 1.0
